// Logisim project Main bus.circ as structural Verilog: 1 circuit, main circuit Main bus
module Main_bus (
);

  Counter #(.width(16), .max('hffff)) counter_1 ();  // open: load, D, count, Q, carry, clk, clr
  RAM ram_1 ();  // open: addr, data, sel, clk, ld, clr

  // Notes on the sheet:
  //   Program counter
  //   RAM
endmodule
